# Fritzing sketch Beruehrungssensor (saved by Fritzing 0.9.1b)
circuit board: 8.46667cm x 5.64444cm
breadboards: 1

parts:
  LM358N = Dual Op-Amp [package=dip08]
  24V_Eingang = Battery
  Probe1 = Screw terminal - 2 pins [package=THT]
  2_2MOhm = Resistor [tolerance=±5% resistance=2.2M package=THT]
  R1 = Resistor [tolerance=±5% resistance=220 package=THT]
  R2 = Resistor [tolerance=±5% resistance=220 package=THT]
  Zum_Arduino = Screw terminal - 2 pins [package=THT]
  LED1 = LED - 5mm [color="Red (633nm)" package="5 mm [THT]"]
  2_2MOhm_2 = Resistor [tolerance=±5% resistance=220 package=THT]
  Probe2 = Screw terminal - 2 pins [package=THT]
  R3 = Resistor [tolerance=±5% resistance=220 package=THT]
  R4 = Resistor [tolerance=±5% resistance=220 package=THT]
  Zum_Arduino_2 = Screw terminal - 2 pins [package=THT]
  LED2 = LED - 5mm [color="Red (633nm)" package="5 mm [THT]"]

nets:
  N1: LM358N.A_OUT, LM358N.A_-IN, R1.Pin_0, Zum_Arduino.pin2
  N2: LM358N.A_+IN, Probe1.pin2, 2_2MOhm.Pin_0
  N3: LM358N.A_V-, LED1.cathode, 2_2MOhm_2.Pin_1, LED2.cathode
  N4: LM358N.B_+IN, 2_2MOhm_2.Pin_0, Probe2.pin2
  N5: LM358N.B_-IN, LM358N.B_OUT, R3.Pin_0, Zum_Arduino_2.pin2
  N6: LM358N.A_V+, 24V_Eingang.-, Probe1.pin1, Probe2.pin1
  N7: 24V_Eingang.+, 2_2MOhm.Pin_1
  N8: R2.Pin_0, Zum_Arduino.pin1
  N9: R2.Pin_1, LED1.anode
  N10: R3.Pin_1, R4.Pin_0, Zum_Arduino_2.pin1
  N11: R4.Pin_1, LED2.anode
